// Logisim project cpu.circ as structural Verilog: 1 circuit, main circuit main
module main (
);

  wire clock_1_out, not_1_out;
  wire [1:0] multiplexer_3_out;
  wire [6:0] bit_extender_1_out;
  wire [7:0] adder_1_out, multiplexer_1_out, multiplexer_2_out, register_1_q, register_2_q;
  wire [15:0] rom_1_data;
  wire [15:8] register_2_q_2;

  Adder adder_1 (.a(multiplexer_2_out), .b(8'h1), .out(adder_1_out));  // open: cin, cout
  Clock clock_1 (.out(clock_1_out));
  // Probe on adder_1_out
  Register register_1 (.D(adder_1_out), .en(clock_1_out), .clk(clock_1_out), .Q(register_1_q));  // open: clr
  // Probe on register_1_q
  // Probe on multiplexer_2_out
  Multiplexer #(.enable("false"), .width(8)) multiplexer_1 (
    .in0(register_1_q), .in1({8{1'b0}}), .out(multiplexer_1_out), .sel(multiplexer_3_out[1]));
  // Probe on register_2_q
  // Probe on multiplexer_1_out
  not not_1 (not_1_out, multiplexer_3_out[1]);
  Button button_1 (.out(multiplexer_3_out[1]));
  // Probe on register_2_q_2[8]
  Multiplexer #(.enable("false"), .select(2), .width(8)) multiplexer_2 (
    .in0(multiplexer_1_out), .in1(register_2_q), .in2({8{1'b0}}), .out(multiplexer_2_out),
    .sel(multiplexer_3_out));  // open: in3
  // Probe on multiplexer_2_out
  Multiplexer #(.enable("false")) multiplexer_3 (
    .in0(1'b0), .in1(register_2_q_2[8]), .out(multiplexer_3_out[0]), .sel(not_1_out));
  // Probe on multiplexer_3_out[0]
  // Probe on multiplexer_2_out
  ROM #(.dataWidth(16)) rom_1 (.addr(multiplexer_2_out), .data(rom_1_data));
  Bit_Extender #(.out_width(7)) bit_extender_1 (.in(register_2_q), .out(bit_extender_1_out));
  // Probe on rom_1_data
  Register #(.width(16)) register_2 (
    .D(rom_1_data), .en(clock_1_out), .clk(clock_1_out), .Q({register_2_q_2, register_2_q}));  // open: clr
  TTY #(.trigger("falling")) tty_1 (
    .data(bit_extender_1_out), .clk(clock_1_out), .clr(multiplexer_3_out[1]));  // open: we

  // Notes on the sheet:
  //   contents of rom_1 (hex, n*v repeats v):
  //   48 45 4c 4c 4f a 100 65 23 33 44 55 7*100
endmodule
